# Fritzing sketch Tweet433MHZ (saved by Fritzing 0.8.7b)
circuit board: 8.46667cm x 5.64444cm

parts:
  CC3K1 = Adafruit CC3000 WiFi Breakout
  Composant1 = Arduino Uno (Rev3) - ICSP

nets:
  GND: CC3K1.GND, Composant1.GND
  VIN: CC3K1.VIN, Composant1.5V
  N1: CC3K1.CLK, Composant1.D13/SCK
  N2: CC3K1.MISO, Composant1.ICSP_MISO, Composant1.D12/MISO
  N3: CC3K1.MOSI, Composant1.ICSP_MOSI, Composant1.D11_PWM/MOSI
  N4: CC3K1.CS, Composant1.D10_PWM/SS
  N5: CC3K1.VBEN, Composant1.D4
  N6: CC3K1.IRQ, Composant1.D3_PWM

custom parts:
  Adafruit CC3000 WiFi Breakout: CC3000 WiFi Breakout
